# Fritzing sketch scale_3.0 (saved by Fritzing 0.9.3b)

parts:
  Часть1 = Arduino Uno (Rev3)  # not connected
  Часть2 = HX711 Weighing Sensor Module
  Часть4 = Memoire 1.0 - SD card log shield
  VCC3 = Battery
  IC1 = Voltage Regulator [package=78xxl]
  S2 = Pushbutton [package=THT]
  LED1 = LEDs [package=led10mm]
  LED2 = LEDs [package=led10mm]
  Part1 = KY-019 5V Relay Module [package="Breakout board"]
  L1 = Inductor [package="0805 [SMD]"]
  VCC4 = Battery

nets:
  N1: Часть2.DO/RX, Часть4.A_IN_1
  N2: Часть2.CK/TX, Часть4.A_IN_0
  N3: Часть4.DIG_9, Part1.S
  N4: Часть4.DIG_6, LED2.C
  N5: Часть4.DIG_7, LED1.C
  N6: Часть4.GND, VCC3.-, Part1.-
  N7: Часть4.VIN, Part1.+
  N8: IC1.IN, S2.leg0
  N9: Part1.NC, L1.pin_0
  N10: Part1.Common, VCC4.+

notes:
  7805
  4AA

custom parts:
  KY-019 5V Relay Module: KY-019 5V Relay module, used to control AC circuits.
  Battery: Your standard 2x 18650 battery pack (7,4 Volts)
